# Fritzing sketch Iris_PI_CO2_Connector (saved by Fritzing 0.9.2b)
breadboards: 1

parts:
  PI2_GPIO_1-10 = Header 5x2 [package=avr_icsp]
  PIXHAWK_TELEM2 = Header 6 [package=molex-1x6_lock]
  CO2_Meter_K30 = Header 5 [package=1x05-1mm]

nets:
  N1: PI2_GPIO_1-10.2, CO2_Meter_K30.3
  N2: PI2_GPIO_1-10.3, CO2_Meter_K30.1
  N3: PI2_GPIO_1-10.4, PIXHAWK_TELEM2.1
  N4: PI2_GPIO_1-10.5, CO2_Meter_K30.2
  N5: PI2_GPIO_1-10.6, PIXHAWK_TELEM2.6
  N6: PI2_GPIO_1-10.8, PIXHAWK_TELEM2.3
  N7: PI2_GPIO_1-10.9, CO2_Meter_K30.4
  N8: PI2_GPIO_1-10.10, PIXHAWK_TELEM2.2

notes:
  Pi2_GPIO1-10
  VCC
  TX
  RX
  RTS
  CTS
  GND
  DVCC 3V3
  3V3
  SDA
  SCL
  G+
  5V
  CLK
